// Logisim project Projects I.circ as structural Verilog
module Basic_Logic_Gates (
  input  A,
  input  B,
  output out_3,
  output out_4,
  output out_5,
  output out_6,
  output out_7,
  output out_8,
  output out_9,
  output out_10
);

  and and_1 (out_3, A, B);
  or or_1 (out_4, A, B);
  not not_1 (out_5, A);
  not not_2 (out_6, B);
  nand nand_1 (out_7, A, B);
  nor nor_1 (out_8, A, B);
  xor xor_1 (out_9, A, B);
  xnor xnor_1 (out_10, A, B);

  // Notes on the sheet:
  //   Basic Logic Gates in Action
endmodule

module Half_Adder (
  input  A,
  input  B,
  output Carry,
  output Sum
);

  and and_1 (Carry, A, B);
  xor xor_1 (Sum, B, A);
endmodule

module Full_Adder (
  input  A,
  input  B,
  input  Cin,
  output Carry,
  output Sum
);

  wire and_1_out, and_2_out, and_3_out, xor_1_out;

  and and_1 (and_1_out, A, B);
  and and_2 (and_2_out, B, Cin);
  or or_1 (Carry, and_1_out, and_2_out, and_3_out);
  and and_3 (and_3_out, A, Cin);
  xor xor_1 (xor_1_out, A, B);
  xor xor_2 (Sum, xor_1_out, Cin);
endmodule

module Half_Subractor (
  input  A,
  input  B,
  output Diff,
  output Borrow
);

  wire not_1_out;

  not not_1 (not_1_out, A);
  xor xor_1 (Diff, B, A);
  and and_1 (Borrow, B, not_1_out);

  // Notes on the sheet:
  //   Half Subractor
endmodule

module Full_Subractor (
  input  A,
  input  B,
  input  C,
  output Diff,
  output Borrow
);

  wire and_1_out, and_2_out, and_3_out, not_1_out, not_2_out, xor_1_out;

  not not_1 (not_1_out, A);
  not not_2 (not_2_out, A);
  xor xor_1 (xor_1_out, C, B);
  and and_1 (and_1_out, C, B);
  and and_2 (and_2_out, C, not_1_out);
  and and_3 (and_3_out, B, not_2_out);
  xor xor_2 (Diff, A, xor_1_out);
  or or_1 (Borrow, and_1_out, and_2_out, and_3_out);

  // Notes on the sheet:
  //   Full Subractor
endmodule

module _3___Bit_Adder_Circuit (
  input  A,
  input  B,
  input  A_2,
  input  B_2,
  input  A_3,
  input  B_3,
  output out_7,
  output out_8,
  output out_9,
  output out_10
);

  wire and_1_out, and_2_out, and_3_out, and_4_out, and_5_out, and_6_out, and_7_out, or_1_out, xor_2_out,
       xor_4_out;

  and and_1 (and_1_out, A, B);
  xor xor_1 (out_10, B, A);
  and and_2 (and_2_out, A_2, B_2);
  and and_3 (and_3_out, A_3, B_3);
  and and_4 (and_4_out, B_2, and_1_out);
  or or_1 (or_1_out, and_2_out, and_4_out, and_7_out);
  and and_5 (and_5_out, A_3, or_1_out);
  and and_6 (and_6_out, B_3, or_1_out);
  or or_2 (out_7, and_3_out, and_6_out, and_5_out);
  and and_7 (and_7_out, A_2, and_1_out);
  xor xor_2 (xor_2_out, A_2, B_2);
  xor xor_3 (out_9, xor_2_out, and_1_out);
  xor xor_4 (xor_4_out, A_3, B_3);
  xor xor_5 (out_8, xor_4_out, or_1_out);

  // Notes on the sheet:
  //   3-Bit Adder Circuit
endmodule

// MUX
module _4_x_1_Multiplexer (
  input  S1,
  input  s0,
  input  Y0,
  input  Y1,
  input  Y2,
  input  Y3,
  output OUT
);

  wire and_1_out, and_2_out, and_3_out, and_4_out, not_1_out, not_2_out;

  not not_1 (not_1_out, S1);
  not not_2 (not_2_out, s0);
  and and_1 (and_1_out, not_1_out, not_2_out, Y0);
  and and_2 (and_2_out, not_1_out, s0, Y1);
  and and_3 (and_3_out, S1, not_2_out, Y2);
  and and_4 (and_4_out, S1, s0, Y3);
  or or_1 (OUT, and_1_out, and_2_out, and_3_out, and_4_out);
endmodule

module _8_x_I_Multiplexer (
  input  S2,
  input  S1,
  input  s0,
  input  Y0,
  input  Y1,
  input  Y2,
  input  Y3,
  input  Y4,
  input  Y5,
  input  Y6,
  input  Y7,
  output out_12
);

  wire and_1_out, and_2_out, and_3_out, and_4_out, and_5_out, and_6_out, and_7_out, and_8_out, not_1_out,
       not_2_out, not_3_out;

  not not_1 (not_1_out, S2);
  not not_2 (not_2_out, S1);
  not not_3 (not_3_out, s0);
  and and_1 (and_1_out, not_1_out, not_2_out, not_3_out, Y0);
  and and_2 (and_2_out, not_1_out, not_2_out, s0, Y1);
  and and_3 (and_3_out, not_1_out, not_3_out, S1, Y2);
  and and_4 (and_4_out, not_1_out, S1, s0, Y3);
  and and_5 (and_5_out, S2, not_2_out, not_3_out, Y4);
  and and_6 (and_6_out, S2, not_2_out, s0, Y5);
  and and_7 (and_7_out, S2, S1, not_3_out, Y6);
  and and_8 (and_8_out, S2, S1, s0, Y7);
  or or_1 (out_12, and_1_out, and_2_out, and_3_out, and_4_out, and_5_out, and_6_out, and_7_out, and_8_out);

  // Notes on the sheet:
  //   8 x 1 Multiplexer
endmodule

module _16_x_1_Multiplexer (
  input  S2,
  input  S2_2,
  input  S1,
  input  s0,
  input  Y0,
  input  Y1,
  input  Y2,
  input  Y3,
  input  Y4,
  input  Y5,
  input  Y6,
  input  Y7,
  input  Y8,
  input  Y9,
  input  Y10,
  input  Y11,
  input  Y12,
  input  Y13,
  input  Y14,
  input  Y15,
  output out_21
);

  wire and_1_out, and_2_out, and_3_out, and_4_out, and_5_out, and_6_out, and_7_out, and_8_out, and_9_out,
       and_10_out, and_11_out, and_12_out, and_13_out, and_14_out, and_15_out, and_16_out, not_1_out,
       not_2_out, not_3_out, not_4_out;

  not not_1 (not_1_out, S2);
  not not_2 (not_2_out, S2_2);
  not not_3 (not_3_out, S1);
  not not_4 (not_4_out, s0);
  and and_1 (and_1_out, not_1_out, not_2_out, not_3_out, not_4_out, Y0);
  and and_2 (and_2_out, not_1_out, not_2_out, not_3_out, s0, Y1);
  and and_3 (and_3_out, not_1_out, not_2_out, S1, not_4_out, Y2);
  and and_4 (and_4_out, not_1_out, not_2_out, S1, s0, Y3);
  and and_5 (and_5_out, not_1_out, S2_2, not_3_out, not_4_out, Y4);
  and and_6 (and_6_out, not_1_out, S2_2, not_3_out, s0, Y5);
  and and_7 (and_7_out, not_1_out, S2_2, S1, not_4_out, Y6);
  and and_8 (and_8_out, not_1_out, S2_2, S1, s0, Y7);
  and and_9 (and_9_out, S2, not_2_out, not_3_out, not_4_out, Y8);
  and and_10 (and_10_out, S2, not_2_out, not_3_out, s0, Y9);
  and and_11 (and_11_out, S2, not_2_out, S1, not_4_out, Y10);
  and and_12 (and_12_out, S2, not_2_out, S1, s0, Y11);
  and and_13 (and_13_out, S2, S2_2, not_3_out, not_4_out, Y12);
  and and_14 (and_14_out, S2, S2_2, not_3_out, s0, Y13);
  and and_15 (and_15_out, S2, S2_2, S1, not_4_out, Y14);
  and and_16 (and_16_out, S2, S2_2, S1, s0, Y15);
  or or_1 (out_21, and_1_out, and_2_out, and_3_out, and_4_out, and_5_out, and_6_out, and_7_out, and_8_out, and_9_out, and_10_out, and_11_out, and_12_out, and_13_out, and_14_out, and_15_out, and_16_out);

  // Notes on the sheet:
  //   16 x 1 Multiplexer
endmodule

// DEMUX
module _1_x_4_Demultiplexer (
  input  IN,
  input  S1,
  input  s0,
  input  _0,
  input  _1,
  input  _2,
  input  _3
);

  wire not_1_out, not_2_out;

  not not_1 (not_1_out, S1);
  not not_2 (not_2_out, s0);
  and and_1 (_0, not_2_out, not_1_out, IN);
  and and_2 (_1, s0, not_1_out, IN);
  and and_3 (_2, not_2_out, S1, IN);
  and and_4 (_3, s0, S1, IN);
endmodule

module _1_x_8_Demultiplexer (
  input  IN,
  input  S2,
  input  S1,
  input  s0
);

  wire and_1_out, and_2_out, and_3_out, and_4_out, and_5_out, and_6_out, and_7_out, and_8_out, not_1_out,
       not_2_out, not_3_out;

  not not_1 (not_1_out, S2);
  not not_2 (not_2_out, S1);
  not not_3 (not_3_out, s0);
  and and_1 (and_1_out, not_3_out, not_2_out, not_1_out, IN);
  and and_2 (and_2_out, s0, not_2_out, not_1_out, IN);
  and and_3 (and_3_out, not_3_out, S1, not_1_out, IN);
  and and_4 (and_4_out, s0, S1, not_1_out, IN);
  and and_5 (and_5_out, not_3_out, not_2_out, S2, IN);
  and and_6 (and_6_out, s0, not_2_out, S2, IN);
  and and_7 (and_7_out, not_3_out, S1, S2, IN);
  and and_8 (and_8_out, s0, S1, S2, IN);

  // Notes on the sheet:
  //   1 x 8 Demultiplexer
endmodule

module _1_x_16_Demultiplexer (
  input  IN,
  input  S3,
  input  S2,
  input  S1,
  input  s0
);

  wire and_1_out, and_2_out, and_3_out, and_4_out, and_5_out, and_6_out, and_7_out, and_8_out, and_9_out,
       and_10_out, and_11_out, and_12_out, and_13_out, and_14_out, and_15_out, and_16_out, not_1_out,
       not_2_out, not_3_out, not_4_out;

  not not_1 (not_1_out, S3);
  not not_2 (not_2_out, S2);
  not not_3 (not_3_out, S1);
  not not_4 (not_4_out, s0);
  and and_1 (and_1_out, not_4_out, not_3_out, not_2_out, not_1_out, IN);
  and and_2 (and_2_out, s0, not_3_out, not_2_out, not_1_out, IN);
  and and_3 (and_3_out, not_4_out, S1, not_2_out, not_1_out, IN);
  and and_4 (and_4_out, s0, S1, not_2_out, not_1_out, IN);
  and and_5 (and_5_out, not_4_out, not_3_out, S2, not_1_out, IN);
  and and_6 (and_6_out, s0, not_3_out, S2, not_1_out, IN);
  and and_7 (and_7_out, not_4_out, S1, S2, not_1_out, IN);
  and and_8 (and_8_out, s0, S1, S2, not_1_out, IN);
  and and_9 (and_9_out, not_4_out, not_3_out, not_2_out, S3, IN);
  and and_10 (and_10_out, s0, not_3_out, not_2_out, S3, IN);
  and and_11 (and_11_out, not_4_out, S1, not_2_out, S3, IN);
  and and_12 (and_12_out, s0, S1, not_2_out, S3, IN);
  and and_13 (and_13_out, not_4_out, not_3_out, S2, S3, IN);
  and and_14 (and_14_out, s0, not_3_out, S2, S3, IN);
  and and_15 (and_15_out, not_4_out, S1, S2, S3, IN);
  and and_16 (and_16_out, s0, S1, S2, S3, IN);

  // Notes on the sheet:
  //   1 x 16 Demultiplexer
endmodule

module _1___Bit_Comparator (
  input  A,
  input  B,
  output Y0___A___B,
  output Y1___A___B,
  output Y2___A___B
);

  wire not_1_out, not_2_out;

  not not_1 (not_1_out, A);
  not not_2 (not_2_out, B);
  and and_1 (Y0___A___B, not_2_out, A);
  xnor xnor_1 (Y1___A___B, B, A);
  and and_2 (Y2___A___B, B, not_1_out);
endmodule

module _2___Bit_Comparator (
  input  A1,
  input  A0,
  input  B1,
  input  B0,
  output Y0,
  output Y1,
  output Y2
);

  wire and_1_out, and_2_out, and_3_out, and_4_out, and_5_out, and_6_out, and_7_out, and_8_out, and_9_out,
       and_10_out, not_1_out, not_2_out, not_3_out, not_4_out;

  not not_1 (not_1_out, A1);
  not not_2 (not_2_out, A0);
  not not_3 (not_3_out, B1);
  not not_4 (not_4_out, B0);
  and and_1 (and_1_out, not_3_out, A1);
  and and_2 (and_2_out, A0, not_3_out, not_4_out);
  and and_3 (and_3_out, not_4_out, A0, A1);
  and and_4 (and_4_out, not_4_out, not_3_out, not_2_out, not_1_out);
  and and_5 (and_5_out, B0, not_3_out, A0, not_1_out);
  and and_6 (and_6_out, not_4_out, B1, not_2_out, A1);
  and and_7 (and_7_out, B0, B1, A0, A1);
  and and_8 (and_8_out, B1, not_1_out);
  and and_9 (and_9_out, B0, B1, not_2_out);
  and and_10 (and_10_out, B0, not_2_out, not_1_out);
  or or_1 (Y0, and_1_out, and_2_out, and_3_out);
  or or_2 (Y1, and_4_out, and_5_out, and_6_out, and_7_out);
  or or_3 (Y2, and_8_out, and_9_out, and_10_out);

  // Notes on the sheet:
  //   Y0 (A > B )
  //   Y1 (A = B)
  //   Y2 (A < B)
endmodule

module _4_x_2_Encoder (
  input  A0,
  input  A1,
  input  A2,
  input  A3,
  output Y1,
  output Y0
);

  or or_1 (Y1, A1, A3);
  or or_2 (Y0, A2, A3);
endmodule

module _8_x_3_Encoder (
  input  A0,
  input  A1,
  input  A2,
  input  A3,
  input  A4,
  input  A5,
  input  A6,
  input  A7,
  output Y0,
  output Y1,
  output Y2
);

  or or_1 (Y0, A1, A3, A5, A7);
  or or_2 (Y1, A2, A3, A6, A7);
  or or_3 (Y2, A4, A5, A6, A7);
endmodule

module _10_x_4_Encoder (
  input  A0,
  input  A1,
  input  A2,
  input  A3,
  input  A4,
  input  A5,
  input  A6,
  input  A7,
  input  A8,
  input  A9,
  output Y0,
  output Y1,
  output Y2,
  output Y3
);

  or or_1 (Y0, A1, A3, A5, A7, A9);
  or or_2 (Y1, A2, A3, A6, A7);
  or or_3 (Y2, A4, A5, A6, A7);
  or or_4 (Y3, A8, A9);
endmodule

module _16_x_4_Encoder (
  input  A0,
  input  A1,
  input  A2,
  input  A3,
  input  A4,
  input  A5,
  input  A6,
  input  A7,
  input  A8,
  input  A9,
  input  A10,
  input  A11,
  input  A12,
  input  A13,
  input  A14,
  input  A15,
  output Y0,
  output Y1,
  output Y2,
  output Y3
);

  or or_1 (Y0, A1, A3, A5, A7, A9, A11, A13, A15);
  or or_2 (Y1, A2, A3, A6, A7, A10, A11, A14, A15);
  or or_3 (Y2, A4, A5, A6, A7, A12, A13, A14, A15);
  or or_4 (Y3, A8, A9, A10, A11, A12, A13, A14, A15);
endmodule

module Priority_Encoder (
  input  D0,
  input  D1,
  input  D2,
  input  D3,
  output Y1,
  output Y0
);

  or or_1 (Y1, D2, D0);
  or or_2 (Y0, D1, D0);
endmodule

module _2_x_4_Decoder (
  input  Y1,
  input  Y0,
  output D0,
  output D1,
  output D2,
  output D3
);

  wire not_1_out, not_2_out;

  not not_1 (not_1_out, Y0);
  not not_2 (not_2_out, Y1);
  and and_1 (D0, not_1_out, not_2_out);
  and and_2 (D1, Y0, not_2_out);
  and and_3 (D2, not_1_out, Y1);
  and and_4 (D3, Y0, Y1);
endmodule

module _3_x_8_Decoder (
  input  Y2,
  input  Y1,
  input  Y0,
  output D0,
  output D1,
  output D2,
  output D3,
  output D4,
  output D5,
  output D6,
  output D7
);

  wire not_1_out, not_2_out, not_3_out;

  not not_1 (not_1_out, Y2);
  not not_2 (not_2_out, Y1);
  not not_3 (not_3_out, Y0);
  and and_1 (D0, not_3_out, not_2_out, not_1_out);
  and and_2 (D1, Y0, not_2_out, not_1_out);
  and and_3 (D2, not_3_out, Y1, not_1_out);
  and and_4 (D3, Y0, Y1, not_1_out);
  and and_5 (D4, not_3_out, not_2_out, Y2);
  and and_6 (D5, Y0, not_2_out, Y2);
  and and_7 (D6, not_3_out, Y1, Y2);
  and and_8 (D7, Y0, Y1, Y2);
endmodule

module _4_x_10_Decoder (
  input  Y3,
  input  Y2,
  input  Y1,
  input  Y0,
  output D0,
  output D1,
  output D2,
  output D3,
  output D4,
  output D5,
  output D6,
  output D7,
  output D8,
  output D9
);

  wire not_1_out, not_2_out, not_3_out, not_4_out;

  not not_1 (not_1_out, Y2);
  not not_2 (not_2_out, Y3);
  not not_3 (not_3_out, Y1);
  not not_4 (not_4_out, Y0);
  and and_1 (D0, not_4_out, not_3_out, not_1_out, not_2_out);
  and and_2 (D1, Y0, not_3_out, not_1_out, not_2_out);
  and and_3 (D2, not_4_out, Y1, not_1_out, not_2_out);
  and and_4 (D3, Y0, Y1, not_1_out, not_2_out);
  and and_5 (D4, not_4_out, not_3_out, Y1, not_2_out);
  and and_6 (D5, Y0, not_3_out, Y2, not_2_out);
  and and_7 (D6, not_4_out, Y1, Y2, not_2_out);
  and and_8 (D7, Y0, Y1, Y2, not_2_out);
  and and_9 (D8, not_4_out, not_3_out, not_1_out, Y3);
  and and_10 (D9, Y0, not_3_out, not_1_out, Y3);
endmodule

module _4_x_16_Decoder (
  input  Y3,
  input  Y2,
  input  Y1,
  input  Y0,
  output D0,
  output D1,
  output D2,
  output D3,
  output D4,
  output D5,
  output D6,
  output D7,
  output D8,
  output D9,
  output D10,
  output D11,
  output D12,
  output D13,
  output D14,
  output D15
);

  wire not_1_out, not_2_out, not_3_out, not_4_out;

  not not_1 (not_1_out, Y2);
  not not_2 (not_2_out, Y3);
  not not_3 (not_3_out, Y1);
  not not_4 (not_4_out, Y0);
  and and_1 (D0, not_4_out, not_3_out, not_1_out, not_2_out);
  and and_2 (D1, Y0, not_3_out, not_1_out, not_2_out);
  and and_3 (D2, not_4_out, Y1, not_1_out, not_2_out);
  and and_4 (D3, Y0, Y1, not_1_out, not_2_out);
  and and_5 (D4, not_4_out, not_3_out, Y1, not_2_out);
  and and_6 (D5, Y0, not_3_out, Y2, not_2_out);
  and and_7 (D6, not_4_out, Y1, Y2, not_2_out);
  and and_8 (D7, Y0, Y1, Y2, not_2_out);
  and and_9 (D8, not_4_out, not_3_out, not_1_out, Y3);
  and and_10 (D9, Y0, not_3_out, not_1_out, Y3);
  and and_11 (D10, not_4_out, Y1, not_1_out, Y3);
  and and_12 (D11, Y0, Y1, not_1_out, Y3);
  and and_13 (D12, not_4_out, not_3_out, Y2, Y3);
  and and_14 (D13, Y0, not_3_out, Y2, Y3);
  and and_15 (D14, not_4_out, Y1, Y2, Y3);
  and and_16 (D15, Y0, Y1, Y2, Y3);
endmodule

module Grey_Code_Converter (
  input  B3,
  input  B2,
  input  B1,
  input  B0
);

  wire not_1_out, not_2_out, not_3_out, not_4_out;

  not not_1 (not_1_out, B3);
  not not_2 (not_2_out, B1);
  not not_3 (not_3_out, B2);
  not not_4 (not_4_out, B0);
  // AND_Gate and_1 is placed but not wired
  // AND_Gate and_2 is placed but not wired
  // AND_Gate and_3 is placed but not wired
  // AND_Gate and_4 is placed but not wired
  // AND_Gate and_5 is placed but not wired
  // AND_Gate and_6 is placed but not wired
  // AND_Gate and_7 is placed but not wired
  // AND_Gate and_8 is placed but not wired
  // AND_Gate and_9 is placed but not wired
  // AND_Gate and_10 is placed but not wired
  // AND_Gate and_11 is placed but not wired
  // AND_Gate and_12 is placed but not wired
  // AND_Gate and_13 is placed but not wired
  // AND_Gate and_14 is placed but not wired
  // AND_Gate and_15 is placed but not wired
  // AND_Gate and_16 is placed but not wired
  // AND_Gate and_17 is placed but not wired
  // AND_Gate and_18 is placed but not wired
  // AND_Gate and_19 is placed but not wired
  // AND_Gate and_20 is placed but not wired
  // AND_Gate and_21 is placed but not wired
  // AND_Gate and_22 is placed but not wired
  // AND_Gate and_23 is placed but not wired
  // AND_Gate and_24 is placed but not wired
  // AND_Gate and_25 is placed but not wired
  // AND_Gate and_26 is placed but not wired
  // AND_Gate and_27 is placed but not wired
  // AND_Gate and_28 is placed but not wired
  // AND_Gate and_29 is placed but not wired
  // AND_Gate and_30 is placed but not wired
  // AND_Gate and_31 is placed but not wired
  // AND_Gate and_32 is placed but not wired
endmodule

module SR_Flip_Flop (
  input  S,
  input  CLK,
  input  R,
  output Qn,
  output Qn_prime
);

  wire nand_1_out, nand_2_out;

  nand nand_1 (nand_1_out, S, CLK);
  nand nand_2 (nand_2_out, CLK, R);
  nand nand_3 (Qn, nand_1_out, Qn_prime);
  nand nand_4 (Qn_prime, Qn, nand_2_out);
endmodule

module D_Flip_Flop (
  input  D,
  input  CLK,
  output Qn,
  output Qn_prime
);

  wire nand_1_out, nand_2_out, not_1_out;

  not not_1 (not_1_out, D);
  nand nand_1 (nand_1_out, D, CLK);
  nand nand_2 (nand_2_out, CLK, not_1_out);
  nand nand_3 (Qn, nand_1_out, Qn_prime);
  nand nand_4 (Qn_prime, Qn, nand_2_out);
endmodule

module JK_Flip_Flop (
  input  J,
  input  CLK,
  input  K,
  output Qn,
  output Qn_prime
);

  wire nand_1_out, nand_2_out;

  nand nand_1 (nand_1_out, Qn_prime, J, CLK);
  nand nand_2 (nand_2_out, CLK, K, Qn);
  nand nand_3 (Qn, nand_1_out, Qn_prime);
  nand nand_4 (Qn_prime, Qn, nand_2_out);
endmodule

module T_Flip_Flop (
  input  D,
  input  CLK,
  output Qn,
  output Qn_prime
);

  wire nand_1_out, nand_2_out, not_1_out;

  not not_1 (not_1_out, D);
  nand nand_1 (nand_1_out, Qn_prime, D, CLK);
  nand nand_2 (nand_2_out, CLK, not_1_out, Qn);
  nand nand_3 (Qn, nand_1_out, Qn_prime);
  nand nand_4 (Qn_prime, Qn, nand_2_out);
endmodule

module Serial_In_Serial_Out_Shift_Register (
  input  Data_IN,
  output Data_OUT
);

  wire CLK_out, D_Flip_Flop_2_q, D_Flip_Flop_3_q, D_Flip_Flop_q;

  Clock CLK (.out(CLK_out));
  D_Flip_Flop_part D_Flip_Flop (.clk(CLK_out), .D(Data_IN), .Q(D_Flip_Flop_q));  // open: Qn, preset, en, reset
  D_Flip_Flop_part D_Flip_Flop_2 (
    .clk(CLK_out), .D(D_Flip_Flop_q), .Q(D_Flip_Flop_2_q));  // open: Qn, preset, en, reset
  D_Flip_Flop_part D_Flip_Flop_3 (
    .clk(CLK_out), .D(D_Flip_Flop_2_q), .Q(D_Flip_Flop_3_q));  // open: Qn, preset, en, reset
  D_Flip_Flop_part D_Flip_Flop_4 (.clk(CLK_out), .D(D_Flip_Flop_3_q), .Q(Data_OUT));  // open: Qn, preset, en, reset
endmodule

module Serial_In_Parallel_Out (
  input  D,
  output out_2,
  output out_3,
  output out_4,
  output out_5
);

  wire CLK_out;

  Clock CLK (.out(CLK_out));
  D_Flip_Flop_part d_ff_1 (.clk(CLK_out), .D(D), .Q(out_2));  // open: Qn, preset, en, reset
  D_Flip_Flop_part d_ff_2 (.clk(CLK_out), .D(out_2), .Q(out_3));  // open: Qn, preset, en, reset
  D_Flip_Flop_part d_ff_3 (.clk(CLK_out), .D(out_3), .Q(out_4));  // open: Qn, preset, en, reset
  D_Flip_Flop_part d_ff_4 (.clk(CLK_out), .D(out_4), .Q(out_5));  // open: Qn, preset, en, reset
endmodule

module Parallel_In_Parallel_Out (
  input  D0,
  input  D1,
  input  D2,
  input  D3,
  output Q0,
  output Q1,
  output Q2,
  output Q3
);

  wire clock_1_out;

  Clock clock_1 (.out(clock_1_out));
  D_Flip_Flop_part D_Flip_Flop (.clk(clock_1_out), .D(D0), .Q(Q0));  // open: Qn, preset, en, reset
  D_Flip_Flop_part D_Flip_Flop_2 (.clk(clock_1_out), .D(D1), .Q(Q1));  // open: Qn, preset, en, reset
  D_Flip_Flop_part D_Flip_Flop_3 (.clk(clock_1_out), .D(D2), .Q(Q2));  // open: Qn, preset, en, reset
  D_Flip_Flop_part D_Flip_Flop_4 (.clk(clock_1_out), .D(D3), .Q(Q3));  // open: Qn, preset, en, reset

  // Notes on the sheet:
  //   Data IN
  //   Data OUT
endmodule

module Parallel_In_Serial_Out (
  input  D0,
  input  D1,
  input  D1_2,
  input  D1_3,
  input  SHIFT___LOAD,
  input  RESET,
  output Q0
);

  wire and_1_out, and_2_out, and_3_out, and_4_out, and_5_out, and_6_out, CLK_out, d_ff_1_q, d_ff_2_q,
       d_ff_3_q, not_1_out, or_1_out, or_2_out, or_3_out;

  Clock CLK (.out(CLK_out));
  not not_1 (not_1_out, SHIFT___LOAD);
  and and_1 (and_1_out, d_ff_1_q, SHIFT___LOAD);
  D_Flip_Flop_part d_ff_1 (.clk(CLK_out), .D(D0), .Q(d_ff_1_q), .reset(RESET));  // open: Qn, preset, en
  and and_2 (and_2_out, not_1_out, D1);
  or or_1 (or_1_out, and_1_out, and_2_out);
  D_Flip_Flop_part d_ff_2 (.clk(CLK_out), .D(or_1_out), .Q(d_ff_2_q), .reset(RESET));  // open: Qn, preset, en
  and and_3 (and_3_out, not_1_out, D1_2);
  and and_4 (and_4_out, d_ff_2_q, SHIFT___LOAD);
  or or_2 (or_2_out, and_4_out, and_3_out);
  D_Flip_Flop_part d_ff_3 (.clk(CLK_out), .D(or_2_out), .Q(d_ff_3_q), .reset(RESET));  // open: Qn, preset, en
  and and_5 (and_5_out, d_ff_3_q, SHIFT___LOAD);
  or or_3 (or_3_out, and_5_out, and_6_out);
  and and_6 (and_6_out, not_1_out, D1_3);
  D_Flip_Flop_part d_ff_4 (.clk(CLK_out), .D(or_3_out), .Q(Q0), .reset(RESET));  // open: Qn, preset, en
endmodule

module _3_Bit_Ripple_UP_counter (
  input  in_1,
  output out_2,
  output out_3,
  output out_4
);

  wire clock_1_out, j_k_ff_1_qn, j_k_ff_2_qn;

  Clock clock_1 (.out(clock_1_out));
  J_K_Flip_Flop j_k_ff_1 (
    .J(in_1), .clk(clock_1_out), .K(in_1), .Q(out_2), .Qn(j_k_ff_1_qn));  // open: preset, en, reset
  J_K_Flip_Flop j_k_ff_2 (
    .J(in_1), .clk(j_k_ff_1_qn), .K(in_1), .Q(out_3), .Qn(j_k_ff_2_qn));  // open: preset, en, reset
  J_K_Flip_Flop j_k_ff_3 (.J(in_1), .clk(j_k_ff_2_qn), .K(in_1), .Q(out_4));  // open: Qn, preset, en, reset
endmodule

module _2_Bit_Ripple_Down_Counter (
  input  in_1,
  output out_2,
  output out_3,
  output out_4
);

  wire clock_1_out;

  Clock clock_1 (.out(clock_1_out));
  J_K_Flip_Flop j_k_ff_1 (.J(in_1), .clk(clock_1_out), .K(in_1), .Qn(out_2));  // open: Q, preset, en, reset
  J_K_Flip_Flop j_k_ff_2 (.J(in_1), .clk(out_2), .K(in_1), .Qn(out_3));  // open: Q, preset, en, reset
  J_K_Flip_Flop j_k_ff_3 (.J(in_1), .clk(out_3), .K(in_1), .Qn(out_4));  // open: Q, preset, en, reset
endmodule

module MOD__5__Counter (
  input  in_1,
  output out_2,
  output out_3,
  output out_4
);

  wire and_1_out, clock_1_out, j_k_ff_1_qn;

  and and_1 (and_1_out, out_4, out_3);
  Clock clock_1 (.out(clock_1_out));
  J_K_Flip_Flop j_k_ff_1 (
    .J(and_1_out), .clk(clock_1_out), .K(in_1), .Q(out_2), .Qn(j_k_ff_1_qn));  // open: preset, en, reset
  J_K_Flip_Flop j_k_ff_2 (.J(out_4), .clk(clock_1_out), .K(out_4), .Q(out_3));  // open: Qn, preset, en, reset
  J_K_Flip_Flop j_k_ff_3 (.J(j_k_ff_1_qn), .clk(clock_1_out), .K(in_1), .Q(out_4));  // open: Qn, preset, en, reset
endmodule

module Arithmetic_Unit (
  input  GND,
  input  S1,
  input  S0,
  input  A1,
  input  A0,
  input  B1,
  input  B0,
  input  in_8
);

  wire not_1_out, not_2_out, not_3_out, not_4_out, not_5_out, not_6_out;

  not not_1 (not_1_out, GND);
  not not_2 (not_2_out, A1);
  not not_3 (not_3_out, A0);
  not not_4 (not_4_out, B1);
  not not_5 (not_5_out, B0);
  not not_6 (not_6_out, in_8);
  _4_x_1_Multiplexer u_4_x_1_multiplexer_1 ();  // open: Y0, Y1, Y2, Y3, S1, s0, OUT
  Full_Adder full_adder_1 ();  // open: A, B, Cin, Carry, Sum
endmodule
